# Fritzing sketch Memory_Game (saved by Fritzing 0.8.7b)
breadboards: 1

parts:
  Microcontroller = TI Launchpad MSP430G2
  LED4 = LED - 5mm [color="Red (633nm)" package="5 mm [THT]"]
  S4 = Pushbutton [package="[THT]"]
  S3 = Pushbutton [package="[THT]"]
  S2 = Pushbutton [package="[THT]"]
  S1 = Pushbutton [package="[THT]"]
  R4 = Resistor [tolerance=±5% resistance=100 package=THT]
  LED3 = LED - 5mm [color="Yellow (595nm)" package="5 mm [THT]"]
  R3 = Resistor [tolerance=±5% resistance=100 package=THT]
  LED2 = LED - 5mm [color="Green (555nm)" package="5 mm [THT]"]
  R2 = Resistor [tolerance=±5% resistance=100 package=THT]
  LED1 = LED - 5mm [color="Blue (430nm)" package="5 mm [THT]"]
  R1 = Resistor [tolerance=±5% resistance=100 package=THT]
  Battery = Battery
  SP1 = SPEAKER [package=pcb_mount_speaker]

nets:
  N1: Microcontroller.p10, S3.Pin_1, S3.Pin_2
  N2: Microcontroller.p9, S2.Pin_1, S2.Pin_2
  N3: Microcontroller.p8, S1.Pin_1, S1.Pin_2
  N4: Microcontroller.p7, LED2.anode
  N5: Microcontroller.p6, LED1.anode
  N6: Microcontroller.p1, Battery.+
  N7: Microcontroller.p11, S4.Pin_1, S4.Pin_2
  N8: Microcontroller.p12, LED4.anode
  N9: Microcontroller.p14, SP1.-
  N10: Microcontroller.p15, LED3.anode
  N11: Microcontroller.p20, S4.Pin_3, S4.Pin_4, S3.Pin_3, S3.Pin_4, S2.Pin_3, S2.Pin_4, S1.Pin_3, S1.Pin_4, R4.Pin_1, R3.Pin_1, R2.Pin_1, R1.Pin_1, Battery.-, SP1.+
  N12: LED4.cathode, R4.Pin_0
  N13: LED3.cathode, R3.Pin_0
  N14: LED2.cathode, R2.Pin_0
  N15: LED1.cathode, R1.Pin_0
